# Fritzing sketch Alarm Clock (saved by Fritzing 1.0.5)

parts:
  Grove1 = Grove 4 Digit Display
  ZS-042_RTC1 = ZS-042 RTC Module
  Part1 = Arduino Uno (Rev3)
  J1 = Piezo Speaker
  R1 = Rotary Potentiometer (Small) [maximum_resistance=100kΩ knob_status=50% power=0.5W package=THT]
  Sensor1 = TTP223B Capacitive Touch Sensor Module
  Sensor2 = TTP223B Capacitive Touch Sensor Module
  Sensor3 = TTP223B Capacitive Touch Sensor Module

nets:
  N1: Grove1.DIO, Part1.D4
  N2: Grove1.CLK, Part1.D3_PWM
  GND: ZS-042_RTC1.GND, Part1.GND
  N3: ZS-042_RTC1.SDA, Part1.A4/SDA
  N4: ZS-042_RTC1.SCL, Part1.A5/SCL
  N5: Part1.A0, R1.wiper
  N6: Part1.D9_PWM, J1.pin2
  N7: Part1.D2, Sensor1.SIG
  N8: Part1.D5_PWM, Sensor3.SIG
  N9: Part1.D6_PWM, Sensor2.SIG
  5V: Part1.5V, Sensor2.VCC

custom parts:
  TTP223B Capacitive Touch Sensor Module: The TTP223B capacitive touch sensor module uses the TTP223B IC. The appropriate voltage is approximately 2 to 5.5 volts.
